# Fritzing sketch arduino_game_schematic (saved by Fritzing 0.9.5d)
breadboards: 1

parts:
  Parte1 = Arduino Uno (Rev3)
  LCD1 = LCD screen
  R1 = Trimmer Potentiometer [maximum_resistance=10kΩ package=THT]
  X1 = USB Connectors [package=usb-microb]
  R2 = Resistor [tolerance=±5% resistance=10k package=THT]
  C1 = Capacitor [package=cap-pth-small2]
  C2 = Capacitor [package=cap-pth-small2]
  C3 = Capacitor [package=cap-pth-small2]
  S1 = Round Pushbutton
  R5 = Resistor [tolerance=±5% resistance=100k package=THT]
  S2 = Round Pushbutton
  S3 = Round Pushbutton
  R6 = Resistor [tolerance=±5% resistance=10k package=THT]
  R7 = Resistor [tolerance=±5% resistance=10k package=THT]
  R8 = Resistor [tolerance=±5% resistance=100k package=THT]
  R9 = Resistor [tolerance=±5% resistance=100k package=THT]

nets:
  N1: Parte1.D9_PWM, C1.2, R7.Pin_1
  N2: Parte1.D11_PWM/MOSI, LCD1.E
  N3: Parte1.D12/MISO, LCD1.RS
  N4: Parte1.D2, LCD1.LED-
  N5: Parte1.D3_PWM, LCD1.LED+
  N6: Parte1.D4, LCD1.DB7
  N7: Parte1.D5_PWM, LCD1.DB6
  N8: Parte1.D6_PWM, R2.Pin_1, C3.2
  N9: Parte1.D7, C2.2, R6.Pin_1
  5V: Parte1.5V, LCD1.VDD, R1.leg2, X1.VBUS, C1.1, C2.1, C3.1, S1.leg1, S2.leg1, S3.leg1
  GND: Parte1.GND, LCD1.VSS, R1.leg1, X1.GND, R5.Pin_1, R8.Pin_1, R9.Pin_1
  N10: LCD1.V0, R1.wiper
  N11: R2.Pin_0, S1.leg0
  N12: S2.leg0, R6.Pin_0, R8.Pin_0
  N13: S3.leg0, R7.Pin_0, R9.Pin_0
